# Fritzing sketch remote2 (saved by Fritzing 0.9.2b)

parts:
  Pwr = Pushbutton [package="[SMD]"]
  Pro_Mini_3V3_8M = Arduino Pro Mini v13
  IR_LED = LEDs [package=led10mm]
  100_Ohms = Resistor [tolerance=±5% resistance=220 package=THT]
  U1 = LIPO-110mAh [package=lipo-110]
  Mute = Pushbutton [package="[SMD]"]
  V+ = Pushbutton [package="[SMD]"]
  V- = Pushbutton [package="[SMD]"]
  Stop = Pushbutton [package="[SMD]"]
  |< = Pushbutton [package="[SMD]"]
  >| = Pushbutton [package="[SMD]"]
  Play = Pushbutton [package="[SMD]"]
  >> = Pushbutton [package="[SMD]"]
  Eject = Pushbutton [package="[SMD]"]
  Phono = Pushbutton [package="[SMD]"]
  Tuner = Pushbutton [package="[SMD]"]
  CD = Pushbutton [package="[SMD]"]
  Line = Pushbutton [package="[SMD]"]
  << = Pushbutton [package="[SMD]"]
  Display = Pushbutton [package="[SMD]"]

nets:
  N1: Pwr.Pin_2, Pro_Mini_3V3_8M.D2, Mute.Pin_1, Mute.Pin_2, V+.Pin_1, V+.Pin_2, V-.Pin_1, V-.Pin_2, Stop.Pin_1, Stop.Pin_2, |<.Pin_1, |<.Pin_2, >|.Pin_2, Play.Pin_2
  N2: Pwr.Pin_3, Pwr.Pin_4, Pro_Mini_3V3_8M.D4, Display.Pin_3, Display.Pin_4
  N3: Pro_Mini_3V3_8M.RAW, U1.+
  N4: Pro_Mini_3V3_8M.GND, IR_LED.A, U1.-
  N5: Pro_Mini_3V3_8M.D12/MISO, Play.Pin_3, Line.Pin_3, Line.Pin_4
  N6: Pro_Mini_3V3_8M.D11_PWM/MOSI, >|.Pin_3, CD.Pin_3, CD.Pin_4
  N7: Pro_Mini_3V3_8M.D10_PWM/SS, |<.Pin_3, Tuner.Pin_3, Tuner.Pin_4
  N8: Pro_Mini_3V3_8M.D9_PWM, 100_Ohms.Pin_1
  N9: Pro_Mini_3V3_8M.D8, Stop.Pin_3, Phono.Pin_3, Phono.Pin_4
  N10: Pro_Mini_3V3_8M.D7, V-.Pin_3, Eject.Pin_3, Eject.Pin_4
  N11: Pro_Mini_3V3_8M.D6_PWM, V+.Pin_3, >>.Pin_3, >>.Pin_4
  N12: Pro_Mini_3V3_8M.D5_PWM, Mute.Pin_3, Mute.Pin_4, <<.Pin_3, <<.Pin_4
  N13: Pro_Mini_3V3_8M.D3_PWM, >>.Pin_2, Eject.Pin_1, Eject.Pin_2, Phono.Pin_1, Phono.Pin_2, Tuner.Pin_2, CD.Pin_2, Line.Pin_1, Line.Pin_2, <<.Pin_1, <<.Pin_2, Display.Pin_1, Display.Pin_2
  N14: IR_LED.C, 100_Ohms.Pin_0
